# Fritzing sketch GreenhouseControler (saved by Fritzing 0.9.2b)
breadboards: 1

parts:
  Part1 = Humidity Sensor - HIH-4030 Breakout
  T1 = LM35 Temperature Sensor [package="TO92 [THT]"]
  Part2 = Arduino Nano (Rev3.0) (ICSP)
  LED1 = RGB LED (com. cathode, rgb) [package="5 mm [THT]"]
  Part3 = Arduino Ethernet Shield (Rev3)  # not connected
  Part5 = Breadboard Power Supply Board SMD
  Part6 = DeadOn RTC - DS3234 Breakout
  Grove1 = Grove OLED 128x96

nets:
  GND: Part1.GND, T1.GND, Part2.GND, LED1.common_cathode, Part5.GND, Part6.GND, Grove1.GND
  N1: Part1.OUT, Part2.A0
  VCC: Part1.VCC, T1.+Vs, Part2.VIN, LED1.red_anode, Part5.VCC, Part6.VCC, Grove1.VCC
  N2: T1.Vout, Part2.A1
  N3: Part2.D2, LED1.blue_anode
  N4: Part2.D3, LED1.green_anode
  N5: Part2.D5, Part6.MOSI
  N6: Part2.D6, Part6.MISO
  N7: Part2.D7, Part6.SCLK
  N8: Part2.D9, Part6.SS
